# Fritzing sketch Moayad-Rafik (saved by Fritzing 0.9.2b)
breadboards: 1

parts:
  D1 = Rectifier Diode [part_number=1N4001 package="300 mil [THT]"]
  R1 = Resistor [tolerance=±5% resistance=220 package=THT]
  LED1 = LED - 5mm [color="Red (633nm)" package="5 mm [THT]"]
  R2 = Resistor [tolerance=±5% resistance=220 package=THT]
  LED2 = LED - 5mm [color="Red (633nm)" package="5 mm [THT]"]
  Q1 = PNP-Transistor [package="TO92 [THT]"]
  R3 = Resistor [tolerance=±5% resistance=220 package=THT]
  R4 = Resistor [tolerance=±5% resistance=220 package=THT]
  LED3 = LED - 5mm [color="Red (633nm)" package="5 mm [THT]"]
  LED4 = LED - 5mm [color="Red (633nm)" package="5 mm [THT]"]
  Part1 = Arduino Uno (Rev3)

nets:
  N1: D1.cathode, Q1.C, Part1.D2
  N2: D1.anode, Q1.E, Part1.D7
  N3: R1.Pin_0, Part1.D8
  N4: R1.Pin_1, LED1.anode
  N5: LED1.cathode, LED2.cathode, LED3.cathode, LED4.cathode, Part1.GND
  N6: R2.Pin_0, Part1.D9_PWM
  N7: R2.Pin_1, LED2.anode
  N8: Q1.B, Part1.D3_PWM
  N9: R3.Pin_0, Part1.D10_PWM/SS
  N10: R3.Pin_1, LED3.anode
  N11: R4.Pin_0, Part1.D11_PWM/MOSI
  N12: R4.Pin_1, LED4.anode
